// Logisim project s-mips.circ as structural Verilog
module S_MIPS_Board (
  input  DESHABILITAR_DISPATCHER,
  output halt
);

  wire button_1_out, CLK, CS, d_ff_1_q, LCLR, LoadRAM, LoadRAMOn, LW, R_R_W, R_W, ram_dispatcher_1_finished,
       RCS, Reset_out, RST, TTY_EN;
  wire [2:0] KDB;
  wire [3:0] LMask, Mask, ram_1_read_time, ram_1_write_time, RMask;
  wire [6:0] KDB_DATA, TTY_DATA;
  wire [15:0] Addr, LAddr, RAddr;
  wire [31:0] I0, I1, I2, I3, LData, ram_1_data_out_0, ram_1_data_out_1, ram_1_data_out_2, ram_1_data_out_3,
       RI0, RI1, RI2, RI3;

  TTY #(.rows(25), .cols(80)) tty_1 (.data(TTY_DATA), .clk(CLK), .we(TTY_EN), .clr(RST));
  not not_1 (LoadRAMOn, ram_dispatcher_1_finished);
  RAM_Dispatcher ram_dispatcher_1 (
    .WriteTime(ram_1_write_time), .Clock(CLK), .Data(LData), .Address(LAddr), .Mask(LMask),
    .Finished(ram_dispatcher_1_finished), .Write(LW), .CLR(LCLR));
  Keyboard #(.buflen(64)) keyboard_1 (.clk(CLK), .re(KDB[0]), .avail(KDB[2]), .data(KDB_DATA));  // open: clr
  RAM ram_1 (
    .Address(RAddr), .Data_Out_0(ram_1_data_out_0), .Data_Out_1(ram_1_data_out_1),
    .Data_Out_2(ram_1_data_out_2), .Data_Out_3(ram_1_data_out_3), .Data_In_0(RI0), .Data_In_1(RI1),
    .Data_In_2(RI2), .Data_In_3(RI3), .Mask(RMask), .nRead_Write(R_R_W), .Chip_Select(RCS),
    .Read_Time(ram_1_read_time), .Reset(button_1_out), .Write_Time(ram_1_write_time));
  Button button_1 (.out(button_1_out));
  D_Flip_Flop d_ff_1 (.clk(CLK), .D(1'b1), .Q(d_ff_1_q), .reset(Reset_out));  // open: Qn, preset, en
  Button Reset (.out(Reset_out));
  S_MIPS s_mips_1 (
    .Kbd_Enable(KDB[0]), .Address(Addr), .Kbd_Clear(KDB[1]), .Kbd_Available(KDB[2]), .RAM_In_0(I0),
    .Kbd_ASCII_Data(KDB_DATA), .RAM_In_1(I1), .TTY_Enable(TTY_EN), .RAM_In_2(I2), .RAM_In_3(I3),
    .TTY_ASCII_Data(TTY_DATA), .Reset(RST), .RAM_Out_0(ram_1_data_out_0), .Clock(CLK),
    .RAM_Out_1(ram_1_data_out_1), .Stop(halt), .RAM_Out_2(ram_1_data_out_2), .RAM_Out_3(ram_1_data_out_3),
    .Mask(Mask), .Read_Time(ram_1_read_time), .Write_Time(ram_1_write_time), .nRead_Write(R_W),
    .Chip_Select(CS));
  D_Flip_Flop d_ff_2 (.clk(CLK), .D(d_ff_1_q), .Qn(LCLR), .reset(Reset_out));  // open: Q, preset, en
  or or_1 (RST, LCLR, LoadRAM);
  Clock clock_1 (.out(CLK));
  Multiplexer #(.width(32), .enable("false")) multiplexer_1 (.in0(I0), .in1(LData), .out(RI0), .sel(LoadRAM));
  Multiplexer #(.width(32), .enable("false")) multiplexer_2 (.in0(I1), .in1(LData), .out(RI1), .sel(LoadRAM));
  Multiplexer #(.width(32), .enable("false")) multiplexer_3 (.in0(I2), .in1(LData), .out(RI2), .sel(LoadRAM));
  Multiplexer #(.width(32), .enable("false")) multiplexer_4 (.in0(I3), .in1(LData), .out(RI3), .sel(LoadRAM));
  and and_1 (LoadRAM, ~DESHABILITAR_DISPATCHER, LoadRAMOn);  // AND_Gate
  Multiplexer #(.width(16), .enable("false")) multiplexer_5 (.in0(Addr), .in1(LAddr), .out(RAddr), .sel(LoadRAM));
  Multiplexer #(.width(4), .enable("false")) multiplexer_6 (.in0(Mask), .in1(LMask), .out(RMask), .sel(LoadRAM));
  Multiplexer #(.enable("false")) multiplexer_7 (.in0(CS), .in1(LW), .out(RCS), .sel(LoadRAM));
  Multiplexer #(.enable("false")) multiplexer_8 (.in0(R_W), .in1(LW), .out(R_R_W), .sel(LoadRAM));

  // Notes on the sheet:
  //   NO MODIFICAR
  //   Keyboard
endmodule

module RAM (
  input  [15:0] Address,
  input  [31:0] Data_In_0,
  input  [31:0] Data_In_1,
  input  [31:0] Data_In_2,
  input  [31:0] Data_In_3,
  input  [3:0] Mask,
  input  nRead_Write,
  input  Chip_Select,
  input  Reset,
  output [31:0] Data_Out_0,
  output [31:0] Data_Out_1,
  output [31:0] Data_Out_2,
  output [31:0] Data_Out_3,
  output [3:0] Read_Time,
  output [3:0] Write_Time
);

  wire and_2_out, and_3_out, and_4_out, and_5_out, and_6_out, and_7_out, and_8_out, and_9_out, Changed, CLK,
       comparator_2_eq, comparator_3_eq, comparator_4_eq, comparator_5_eq, comparator_6_eq, Count,
       demultiplexer_3_out0, Idle, Idle_q, Load, Load0, Load1, nand_1_out, or_1_out, or_2_out, or_3_out,
       or_4_out, or_5_out, or_6_out, or_7_out, or_8_out, or_9_out, or_10_out, Proc_q, Update_Mem, Zero_Time;
  wire [3:0] counter_1_q, multiplexer_1_out, subtractor_1_out;
  wire [31:0] register_1_q, register_2_q, register_3_q, register_4_q, register_5_q;

  // Probe on 4'b0011
  // Probe on 4'b0010
  Multiplexer #(.width(4), .enable("false")) multiplexer_1 (
    .in0(4'b0011), .in1(4'b0010), .out(multiplexer_1_out), .sel(nRead_Write));
  or or_1 (or_1_out, Idle, Update_Mem);
  or or_2 (or_2_out, ~Chip_Select, Reset);  // OR_Gate
  Subtractor #(.width(4)) subtractor_1 (.a(multiplexer_1_out), .b(4'b0010), .out(subtractor_1_out));  // open: bin, bout
  Demultiplexer #(.enable("false")) demultiplexer_1 (.out0(Idle), .out1(Load0), .in(Idle_q), .sel(Changed));
  D_Flip_Flop u_Idle (.clk(CLK), .D(or_1_out), .Q(Idle_q), .preset(or_2_out));  // open: Qn, en, reset
  // Probe on counter_1_q
  Counter #(.width(4), .max('hf)) counter_1 (
    .load(Load), .D(subtractor_1_out), .count(Count), .Q(counter_1_q), .clk(CLK), .clr(or_3_out));  // open: carry
  or or_3 (or_3_out, ~Chip_Select, Reset);  // OR_Gate
  Comparator #(.width(4), .mode("unsigned")) comparator_1 (
    .a(4'b0000), .b(counter_1_q), .eq(Zero_Time));  // open: gt, lt
  or or_4 (or_4_out, Count, Load0, Load1);
  Register #(.width(32)) register_1 (.D(Data_In_0), .en(Chip_Select), .Q(register_1_q), .clk(CLK), .clr(or_5_out));
  or or_5 (or_5_out, ~Chip_Select, Reset);  // OR_Gate
  Register #(.width(32)) register_2 (.D(Data_In_1), .en(Chip_Select), .Q(register_2_q), .clk(CLK), .clr(or_6_out));
  or or_6 (or_6_out, ~Chip_Select, Reset);  // OR_Gate
  Register #(.width(32)) register_3 (.D(Data_In_2), .en(Chip_Select), .Q(register_3_q), .clk(CLK), .clr(or_7_out));
  or or_7 (or_7_out, ~Chip_Select, Reset);  // OR_Gate
  Register #(.width(32)) register_4 (.D(Data_In_3), .en(Chip_Select), .Q(register_4_q), .clk(CLK), .clr(or_8_out));
  or or_8 (or_8_out, ~Chip_Select, Reset);  // OR_Gate
  Register #(.width(32)) register_5 (
    .D({{11{1'b1}}, nRead_Write, Mask, Address}), .en(Chip_Select), .Q(register_5_q), .clk(CLK),
    .clr(or_9_out));
  or or_9 (or_9_out, ~Chip_Select, Reset);  // OR_Gate
  D_Flip_Flop Proc (.clk(CLK), .D(or_4_out), .Q(Proc_q), .reset(or_10_out));  // open: Qn, preset, en
  or or_10 (or_10_out, ~Chip_Select, Reset);  // OR_Gate
  Demultiplexer #(.enable("false")) demultiplexer_2 (
    .out0(Count), .out1(Update_Mem), .in(demultiplexer_3_out0), .sel(Zero_Time));
  Demultiplexer #(.enable("false")) demultiplexer_3 (
    .out0(demultiplexer_3_out0), .out1(Load1), .in(Proc_q), .sel(Changed));
  Clock clock_1 (.out(CLK));
  Comparator #(.width(32)) comparator_2 (.a(register_1_q), .b(Data_In_0), .eq(comparator_2_eq));  // open: gt, lt
  Comparator #(.width(32)) comparator_3 (.a(register_2_q), .b(Data_In_1), .eq(comparator_3_eq));  // open: gt, lt
  Comparator #(.width(32)) comparator_4 (.a(register_3_q), .b(Data_In_2), .eq(comparator_4_eq));  // open: gt, lt
  Comparator #(.width(32)) comparator_5 (.a(register_4_q), .b(Data_In_3), .eq(comparator_5_eq));  // open: gt, lt
  Comparator #(.width(32)) comparator_6 (
    .a(register_5_q), .b({{11{1'b1}}, nRead_Write, Mask, Address}), .eq(comparator_6_eq));  // open: gt, lt
  nand nand_1 (nand_1_out, comparator_6_eq, comparator_2_eq, comparator_3_eq, comparator_4_eq, comparator_5_eq);
  and and_1 (Changed, nand_1_out, Chip_Select);
  or or_11 (Load, Count, Load1, Load0);
  and and_2 (and_2_out, Mask[0], Update_Mem, nRead_Write);
  and and_3 (and_3_out, Mask[1], Update_Mem, nRead_Write);
  and and_4 (and_4_out, Mask[2], Update_Mem, nRead_Write);
  and and_5 (and_5_out, Mask[3], Update_Mem, nRead_Write);
  RAM_part #(.addrWidth(16), .dataWidth(32), .bus("separate")) ram_1 (
    .addr(Address), .din(Data_In_0), .data(Data_Out_0), .str(and_2_out), .sel(Chip_Select), .clk(CLK),
    .ld(and_6_out), .clr(Reset));
  and and_6 (and_6_out, ~nRead_Write, Idle);  // AND_Gate
  RAM_part #(.addrWidth(16), .dataWidth(32), .bus("separate")) ram_2 (
    .addr(Address), .din(Data_In_1), .data(Data_Out_1), .str(and_3_out), .sel(Chip_Select), .clk(CLK),
    .ld(and_7_out), .clr(Reset));
  and and_7 (and_7_out, ~nRead_Write, Idle);  // AND_Gate
  RAM_part #(.addrWidth(16), .dataWidth(32), .bus("separate")) ram_3 (
    .addr(Address), .din(Data_In_2), .data(Data_Out_2), .str(and_4_out), .sel(Chip_Select), .clk(CLK),
    .ld(and_8_out), .clr(Reset));
  and and_8 (and_8_out, ~nRead_Write, Idle);  // AND_Gate
  RAM_part #(.addrWidth(16), .dataWidth(32), .bus("separate")) ram_4 (
    .addr(Address), .din(Data_In_3), .data(Data_Out_3), .str(and_5_out), .sel(Chip_Select), .clk(CLK),
    .ld(and_9_out), .clr(Reset));
  and and_9 (and_9_out, ~nRead_Write, Idle);  // AND_Gate

  assign Read_Time = 4'b0011;
  assign Write_Time = 4'b0010;

  // Other names for the same wires on the sheet: M0 = Mask[0]; M1 = Mask[1]; M2 = Mask[2]; M3 = Mask[3];
  //   RW = nRead_Write; CLR = Reset; CS = Chip_Select; Load2 = Count

  // Notes on the sheet:
  //   NO MODIFICAR
  //   excepto quizás los valores RT y WT
  //   BANK0
  //   BANK1
  //   BANK2
  //   BANK3
endmodule

module S_MIPS (
  input  Kbd_Available,
  input  [6:0] Kbd_ASCII_Data,
  input  [31:0] RAM_Out_0,
  input  [31:0] RAM_Out_1,
  input  Reset,
  input  [31:0] RAM_Out_2,
  input  Clock,
  input  [31:0] RAM_Out_3,
  input  [3:0] Read_Time,
  input  [3:0] Write_Time,
  output Kbd_Enable,
  output [15:0] Address,
  output Kbd_Clear,
  output TTY_Enable,
  output [6:0] TTY_ASCII_Data,
  output Stop,
  output [31:0] RAM_In_0,
  output [31:0] RAM_In_1,
  output [31:0] RAM_In_2,
  output [31:0] RAM_In_3,
  output [3:0] Mask,
  output nRead_Write,
  output Chip_Select
);

  wire control_unit_1_out_11, control_unit_1_out_12, control_unit_1_out_14, control_unit_1_out_17,
       control_unit_1_out_18, control_unit_1_out_20, control_unit_1_out_24, Data, Hit, RW_Chache,
       start_Chache, xor_1_out;
  wire [1:0] AddS, control_unit_1_out_9, control_unit_1_out_15;
  wire [2:0] control_unit_1_out_7, control_unit_1_out_13, DS;
  wire [5:0] Func_Code, Op_Code;
  wire [31:0] Adr, DP, Ram;

  Control_Unit_2 control_unit_1 (
    .OpCode(Op_Code), .FuncCode(Func_Code), .rst(Reset), .Clock(Clock), .in_5(Hit), .out_16(Stop),
    .out_17(control_unit_1_out_17), .out_19(RW_Chache), .out_9(control_unit_1_out_9),
    .out_15(control_unit_1_out_15), .out_7(control_unit_1_out_7), .out_22(start_Chache), .out_23(Kbd_Enable),
    .out_21(TTY_Enable), .out_13(control_unit_1_out_13), .out_12(control_unit_1_out_12),
    .out_14(control_unit_1_out_14), .out_10(AddS), .out_8(DS), .out_18(control_unit_1_out_18),
    .out_24(control_unit_1_out_24), .out_20(control_unit_1_out_20), .out_11(control_unit_1_out_11),
    .in_6(Data));
  xor xor_1 (xor_1_out, AddS[0], AddS[1]);
  Data_Path_2 data_path_1 (
    .RAM(Ram), .Clock(Clock), .Reset(Reset), .W_PC(control_unit_1_out_20), .W_Inst(control_unit_1_out_11),
    .R_W_RF(control_unit_1_out_18), .R_W_HL(control_unit_1_out_17), .R_W_SP(control_unit_1_out_24),
    .Data_Output_Selector(control_unit_1_out_12), .RegDST(control_unit_1_out_14), .BS(control_unit_1_out_9),
    .Branch_Type_Selector(control_unit_1_out_15), .ALU_OP(control_unit_1_out_7),
    .Flag_Selector(control_unit_1_out_13), .Data_Selector(DS), .KBD_Data(Kbd_ASCII_Data), .Address(Adr),
    .Write_Data(DP), .tty_out(TTY_ASCII_Data), .Opcode(Op_Code), .FuncCode(Func_Code),
    .KBD_Available(Kbd_Available), .Address_selector(AddS));
  Cache cache_1 (
    .Clk(Clock), .Read_Time(Read_Time), .Rst(Reset), .Write_Time(Write_Time), .start(start_Chache),
    .nR_W_Ram(RW_Chache), .Adr(Adr), .In0(RAM_Out_0), .In1(RAM_Out_1), .In2(RAM_Out_2), .In3(RAM_Out_3),
    .Data_Path(DP), .IorD(xor_1_out), .RAM_Out(Ram), .Address(Address), .Hit_Instruction(Hit),
    .Out0(RAM_In_0), .Out1(RAM_In_1), .Out2(RAM_In_2), .Out3(RAM_In_3), .Mask(Mask), .CS(Chip_Select),
    .RW(nRead_Write), .Hit_Data(Data));

  assign Kbd_Clear = Reset;

  // Other names for the same wires on the sheet: CLK = Clock; CS = Chip_Select; KBD_AVAIL = Kbd_Available;
  //   CLR = Reset; KBD_CLR = Reset; KBD_DATA[6:0] = Kbd_ASCII_Data; RAM_A[15:0] = Address;
  //   RAM_INPUT_0[31:0] = RAM_In_0; RAM_INPUT_1[31:0] = RAM_In_1; RAM_INPUT_2[31:0] = RAM_In_2;
  //   RAM_INPUT_3[31:0] = RAM_In_3; RAM_MASK[3:0] = Mask; RAM_OUTPUT_0[31:0] = RAM_Out_0;
  //   RAM_OUTPUT_1[31:0] = RAM_Out_1; RAM_OUTPUT_2[31:0] = RAM_Out_2; RAM_OUTPUT_3[31:0] = RAM_Out_3;
  //   RW = nRead_Write; TTY_DATA[6:0] = TTY_ASCII_Data

  // Notes on the sheet:
  //   RAM ADDRESS
  //   DATA FROM RAM
  //   DATA TO RAM
  //   DATA WRITE MASK
  //   RAM TIMING
  //   RAM CONTROL
  //   KEYBOARD
  //   TTY
  //   SEQUENCING
endmodule

module RAM_Dispatcher (
  input  [3:0] WriteTime,
  input  Clock,
  input  CLR,
  output [31:0] Data,
  output [15:0] Address,
  output [3:0] Mask,
  output Finished,
  output Write
);

  wire demultiplexer_2_out1, demultiplexer_3_out1, End, IDLE_q, IncAddr, Load, or_1_out, or_2_out, While_q,
       WriteEnd;
  wire [3:0] counter_1_q;
  wire [31:0] CurrentAddress_q;

  Counter #(.width(32), .max('hffffffff)) CurrentAddress (
    .count(IncAddr), .Q({CurrentAddress_q[31:18], Address, CurrentAddress_q[1:0]}), .clk(Clock), .clr(CLR));  // open: load, D, carry
  or or_1 (or_1_out, IncAddr, demultiplexer_3_out1, Finished);
  D_Flip_Flop IDLE (.clk(Clock), .D(or_1_out), .Q(IDLE_q), .preset(CLR));  // open: Qn, en, reset
  Demultiplexer #(.enable("false")) demultiplexer_1 (.out0(Load), .out1(Finished), .in(IDLE_q), .sel(End));
  D_Flip_Flop While (.clk(Clock), .D(or_2_out), .Q(While_q), .reset(CLR));  // open: Qn, preset, en
  or or_2 (or_2_out, Write, Load);
  RAM_part #(.addrWidth(18), .dataWidth(32)) ram_1 (
    .addr({Address, CurrentAddress_q[1:0]}), .data(Data), .clk(Clock));  // open: sel, ld, clr
  Demultiplexer #(.enable("false")) demultiplexer_2 (
    .out0(Write), .out1(demultiplexer_2_out1), .in(While_q), .sel(WriteEnd));
  Decoder #(.select(2)) decoder_1 (
    .out0(Mask[0]), .out1(Mask[1]), .out2(Mask[2]), .out3(Mask[3]), .sel(CurrentAddress_q[1:0]));  // open: en
  Demultiplexer #(.enable("false")) demultiplexer_3 (
    .out0(IncAddr), .out1(demultiplexer_3_out1), .in(demultiplexer_2_out1), .sel(End));
  Counter #(.width(4), .max('hf)) counter_1 (
    .load(Load), .D(WriteTime), .count(Write), .Q(counter_1_q), .clk(Clock));  // open: carry, clr
  Comparator #(.width(32)) comparator_1 (.a(Data), .b({32{1'b1}}), .eq(End));  // open: gt, lt
  Comparator #(.width(4)) comparator_2 (.a(4'b0000), .b(counter_1_q), .eq(WriteEnd));  // open: gt, lt

  // Other names for the same wires on the sheet: CLK = Clock; Count = Write; WT[3:0] = WriteTime
endmodule

module Data_Path_2 (
  input  [31:0] RAM,
  input  Clock,
  input  Reset,
  input  W_PC,
  input  W_Inst,
  input  R_W_RF,
  input  R_W_HL,
  input  R_W_SP,
  input  Data_Output_Selector,
  input  RegDST,
  input  [1:0] Address_selector,
  input  [1:0] BS,
  input  [1:0] Branch_Type_Selector,
  input  [2:0] ALU_OP,
  input  [2:0] Flag_Selector,
  input  [2:0] Data_Selector,
  input  [6:0] KBD_Data,
  input  KBD_Available,
  output [31:0] Address,
  output [31:0] Write_Data,
  output [6:0] tty_out,
  output [5:0] Opcode,
  output [5:0] FuncCode
);

  wire N, P_P, Z;
  wire [4:0] DataAdd, RD_Selector, RS_Selector, RT_Selector;
  wire [25:0] Target;
  wire [31:0] B, bit_extender_1_out, DataIn, Hi, Hi_In, Kbd, Lo, Lo_In, multiplexer_2_out, PC, PC_prime, R,
       Rnd, Signed_Constant, SP, Unsigned_Constant;
  wire [31:7] RS;

  // Probe on PC_prime
  assign bit_extender_1_out = {{25{1'b0}}, KBD_Data};  // Bit_Extender bit_extender_1
  Register #(.width(32)) u_PC (.D(PC_prime), .en(W_PC), .Q(PC), .clk(Clock), .clr(Reset));
  and and_1 (P_P, BS[0], BS[1], ~ALU_OP[0], ~ALU_OP[1], ~ALU_OP[2]);  // AND_Gate
  Multiplexer #(.width(32)) multiplexer_1 (
    .in0({32{1'b1}}), .in1(bit_extender_1_out), .out(Kbd), .sel(KBD_Available));  // open: en
  Random #(.width(32)) u_RND (.clk(Clock), .out(Rnd));  // open: next, clr
  Instruction_Splitter instruction_splitter_1 (
    .Instruction(RAM), .Clk(Clock), .Reset(Reset), .Instruction_Memory_R_W(W_Inst), .OpCode(Opcode),
    .Rs(RS_Selector), .Rt(RT_Selector), .Rd(RD_Selector), .FuncCode(FuncCode), .Jump_Target(Target),
    .Unsigned_Const(Unsigned_Constant), .Signed_Const(Signed_Constant));
  Register_File register_file_1 (
    .In(DataIn), .Sa(RS_Selector), .Sb(RT_Selector), .W_R(R_W_RF), .DA(DataAdd), .Hi(Hi_In), .Lo(Lo_In),
    .Clk(Clock), .Rst(Reset), .HL_R_W(R_W_HL), .SP_R_W(R_W_SP), .A_out({RS, tty_out}), .B_out(B), .Hi_2(Hi),
    .Lo_2(Lo), .SP_Output(SP), .push_pop(P_P));
  Multiplexer #(.select(2), .width(32)) multiplexer_2 (
    .in0(B), .in1(Signed_Constant), .in2(Unsigned_Constant), .in3({32{1'b0}}), .out(multiplexer_2_out),
    .sel(BS));  // open: en
  Branch_Control branch_control_1 (
    .PC(PC), .Target(Target), .Const(Signed_Constant), .Register_Value({RS, tty_out}),
    .Branch_Type_Selector(Branch_Type_Selector), .Flag_Selector(Flag_Selector), .Zero_Flag(Z),
    .Negative_Flag(N), .PC_prime(PC_prime));
  Multiplexer #(.width(5)) multiplexer_3 (
    .in0(RD_Selector), .in1(RT_Selector), .out(DataAdd), .sel(RegDST));  // open: en
  ALU alu_1 (
    .A({RS, tty_out}), .B(multiplexer_2_out), .Op(ALU_OP), .Result(R), .Lo(Lo_In), .Hi(Hi_In), .Zero(Z),
    .Negative(N));
  Multiplexer #(.select(3), .width(32)) multiplexer_4 (
    .in0(R), .in1(RAM), .in3(Lo), .in5(Hi), .in6(Rnd), .in7(Kbd), .out(DataIn), .sel(Data_Selector));  // open: in2, in4, en
  Multiplexer #(.select(2), .width(32)) multiplexer_5 (
    .in0(PC), .in1(R), .in2(SP), .out(Address), .sel(Address_selector));  // open: in3, en
  Multiplexer #(.width(32)) multiplexer_6 (
    .in0(B), .in1({RS, tty_out}), .out(Write_Data), .sel(Data_Output_Selector));  // open: en

  // Other names for the same wires on the sheet: AS[1:0] = Address_selector; BTS[1:0] = Branch_Type_Selector;
  //   Clk = Clock; DOS = Data_Output_Selector; DS[2:0] = Data_Selector; FS[2:0] = Flag_Selector; RS[6:0] = tty_out;
  //   Rst = Reset
endmodule

module Register_File (
  input  [31:0] In,
  input  [4:0] Sa,
  input  [4:0] Sb,
  input  W_R,
  input  [4:0] DA,
  input  [31:0] Hi,
  input  [31:0] Lo,
  input  Clk,
  input  Rst,
  input  HL_R_W,
  input  push_pop,
  input  SP_R_W,
  output [31:0] A_out,
  output [31:0] B_out,
  output [31:0] Hi_2,
  output [31:0] Lo_2,
  output [31:0] SP_Output
);

  wire SP_EN, W_R1, W_R2, W_R3, W_R4, W_R5, W_R6, W_R7, W_R8, W_R9, W_R10, W_R11, W_R12, W_R13, W_R14, W_R15,
       W_R16, W_R17, W_R18, W_R19, W_R20, W_R21, W_R22, W_R23, W_R24, W_R25, W_R26, W_R27, W_R28, W_R29,
       W_R30, W_R31;
  wire [31:0] adder_1_out, multiplexer_1_out, R1, R2, R3, R4, R5, R6, R7, R8, R9, R10, R11, R12, R13, R14,
       R15, R16, R17, R18, R19, R20, R21, R22, R23, R24, R25, R26, R27, R28, R29, R30, SP_In;

  Demultiplexer #(.select(5), .enable("false")) demultiplexer_1 (
    .out1(W_R1), .out2(W_R2), .out3(W_R3), .out4(W_R4), .out5(W_R5), .out6(W_R6), .out7(W_R7), .out8(W_R8),
    .out9(W_R9), .out10(W_R10), .out11(W_R11), .out12(W_R12), .out13(W_R13), .out14(W_R14), .out15(W_R15),
    .out16(W_R16), .out17(W_R17), .out18(W_R18), .out19(W_R19), .out20(W_R20), .out21(W_R21), .out22(W_R22),
    .out23(W_R23), .out24(W_R24), .out25(W_R25), .out26(W_R26), .out27(W_R27), .out28(W_R28), .out29(W_R29),
    .out30(W_R30), .out31(W_R31), .in(W_R), .sel(DA));  // open: out0
  or or_1 (SP_EN, W_R31, SP_R_W);
  Register #(.width(32)) register_1 (.D(Hi), .en(HL_R_W), .Q(Hi_2), .clk(Clk), .clr(Rst));
  Register #(.width(32)) register_2 (.D(Lo), .en(HL_R_W), .Q(Lo_2), .clk(Clk), .clr(Rst));
  Multiplexer #(.width(32)) multiplexer_1 (
    .in0(32'hfffffffc), .in1(32'h4), .out(multiplexer_1_out), .sel(push_pop));  // open: en
  Register #(.width(32)) register_3 (.D(In), .en(W_R1), .Q(R1), .clk(Clk), .clr(Rst));
  Register #(.width(32)) register_4 (.D(In), .en(W_R2), .Q(R2), .clk(Clk), .clr(Rst));
  Register #(.width(32)) register_5 (.D(In), .en(W_R3), .Q(R3), .clk(Clk), .clr(Rst));
  Register #(.width(32)) register_6 (.D(In), .en(W_R4), .Q(R4), .clk(Clk), .clr(Rst));
  Register #(.width(32)) register_7 (.D(In), .en(W_R5), .Q(R5), .clk(Clk), .clr(Rst));
  Register #(.width(32)) register_8 (.D(In), .en(W_R6), .Q(R6), .clk(Clk), .clr(Rst));
  Register #(.width(32)) register_9 (.D(In), .en(W_R7), .Q(R7), .clk(Clk), .clr(Rst));
  Adder #(.width(32)) adder_1 (.a(multiplexer_1_out), .b(SP_Output), .out(adder_1_out));  // open: cin, cout
  Multiplexer #(.width(32)) multiplexer_2 (.in0(In), .in1(adder_1_out), .out(SP_In), .sel(SP_R_W));  // open: en
  Register #(.width(32)) register_10 (.D(In), .en(W_R8), .Q(R8), .clk(Clk), .clr(Rst));
  Register #(.width(32)) register_11 (.D(In), .en(W_R9), .Q(R9), .clk(Clk), .clr(Rst));
  Register #(.width(32)) register_12 (.D(In), .en(W_R10), .Q(R10), .clk(Clk), .clr(Rst));
  Register #(.width(32)) register_13 (.D(In), .en(W_R11), .Q(R11), .clk(Clk), .clr(Rst));
  Register #(.width(32)) register_14 (.D(In), .en(W_R12), .Q(R12), .clk(Clk), .clr(Rst));
  Register #(.width(32)) register_15 (.D(In), .en(W_R13), .Q(R13), .clk(Clk), .clr(Rst));
  Register #(.width(32)) register_16 (.D(In), .en(W_R14), .Q(R14), .clk(Clk), .clr(Rst));
  Register #(.width(32)) register_17 (.D(In), .en(W_R15), .Q(R15), .clk(Clk), .clr(Rst));
  Register #(.width(32)) register_18 (.D(In), .en(W_R16), .Q(R16), .clk(Clk), .clr(Rst));
  Register #(.width(32)) register_19 (.D(In), .en(W_R17), .Q(R17), .clk(Clk), .clr(Rst));
  Register #(.width(32)) register_20 (.D(In), .en(W_R18), .Q(R18), .clk(Clk), .clr(Rst));
  Register #(.width(32)) register_21 (.D(In), .en(W_R19), .Q(R19), .clk(Clk), .clr(Rst));
  Register #(.width(32)) register_22 (.D(In), .en(W_R20), .Q(R20), .clk(Clk), .clr(Rst));
  Register #(.width(32)) register_23 (.D(In), .en(W_R21), .Q(R21), .clk(Clk), .clr(Rst));
  Register #(.width(32)) register_24 (.D(In), .en(W_R22), .Q(R22), .clk(Clk), .clr(Rst));
  Register #(.width(32)) register_25 (.D(In), .en(W_R23), .Q(R23), .clk(Clk), .clr(Rst));
  Register #(.width(32)) register_26 (.D(In), .en(W_R24), .Q(R24), .clk(Clk), .clr(Rst));
  Register #(.width(32)) register_27 (.D(In), .en(W_R25), .Q(R25), .clk(Clk), .clr(Rst));
  Register #(.width(32)) register_28 (.D(In), .en(W_R26), .Q(R26), .clk(Clk), .clr(Rst));
  Register #(.width(32)) register_29 (.D(In), .en(W_R27), .Q(R27), .clk(Clk), .clr(Rst));
  Register #(.width(32)) register_30 (.D(In), .en(W_R28), .Q(R28), .clk(Clk), .clr(Rst));
  Register #(.width(32)) register_31 (.D(In), .en(W_R29), .Q(R29), .clk(Clk), .clr(Rst));
  Register #(.width(32)) register_32 (.D(In), .en(W_R30), .Q(R30), .clk(Clk), .clr(Rst));
  Register #(.width(32)) register_33 (.D(SP_In), .en(SP_EN), .Q(SP_Output), .clk(Clk), .clr(Rst));
  Multiplexer #(.select(5), .width(32)) multiplexer_3 (
    .in0({32{1'b0}}), .in1(R1), .in2(R2), .in3(R3), .in4(R4), .in5(R5), .in6(R6), .in7(R7), .in8(R8),
    .in9(R9), .in10(R10), .in11(R11), .in12(R12), .in13(R13), .in14(R14), .in15(R15), .in16(R16), .in17(R17),
    .in18(R18), .in19(R19), .in20(R20), .in21(R21), .in22(R22), .in23(R23), .in24(R24), .in25(R25),
    .in26(R26), .in27(R27), .in28(R28), .in29(R29), .in30(R30), .in31(SP_Output), .out(A_out), .sel(Sa));  // open: en
  Multiplexer #(.select(5), .width(32)) multiplexer_4 (
    .in0({32{1'b0}}), .in1(R1), .in2(R2), .in3(R3), .in4(R4), .in5(R5), .in6(R6), .in7(R7), .in8(R8),
    .in9(R9), .in10(R10), .in11(R11), .in12(R12), .in13(R13), .in14(R14), .in15(R15), .in16(R16), .in17(R17),
    .in18(R18), .in19(R19), .in20(R20), .in21(R21), .in22(R22), .in23(R23), .in24(R24), .in25(R25),
    .in26(R26), .in27(R27), .in28(R28), .in29(R29), .in30(R30), .in31(SP_Output), .out(B_out), .sel(Sb));  // open: en

  // Other names for the same wires on the sheet: Hi_In[31:0] = Hi; Hi_t[31:0] = Hi_2; Lo_In[31:0] = Lo;
  //   Lo_t[31:0] = Lo_2; SP_Out[31:0] = SP_Output

  // Notes on the sheet:
  //   Inputs
  //   Select register to write
  //   Lo Hi
  //   Registers R0-R31
  //   Output selector
  //   Output
endmodule

module ALU (
  input  [31:0] A,
  input  [31:0] B,
  input  [2:0] Op,
  output [31:0] Result,
  output Zero,
  output Negative,
  output [31:0] Lo,
  output [31:0] Hi
);

  wire comparator_1_lt, comparator_2_lt;
  wire [31:0] add, \and , div_Hi, div_Lo, divu_Hi, divu_Lo, mult_Hi, mult_Lo, mulu_Hi, mulu_Lo, \nor , \or ,
       slt, sltu, sub, \xor ;

  Adder #(.width(32)) adder_1 (.a(A), .b(B), .out(add));  // open: cin, cout
  Subtractor #(.width(32)) subtractor_1 (.a(A), .b(B), .out(sub));  // open: bin, bout
  assign \xor  = A ^ B;  // XOR_Gate xor_1, 32 bits wide
  assign \or  = A | B;  // OR_Gate or_1, 32 bits wide
  assign \nor  = ~\or ;  // NOT_Gate not_1, 32 bits wide
  assign \and  = A & B;  // AND_Gate and_1, 32 bits wide
  Multiplier #(.width(32)) multiplier_1 (.a(A), .b(B), .out(mulu_Lo), .cout(mulu_Hi));  // open: cin
  Signed_Multiplication signed_multiplication_1 (.A(A), .B(B), .Lo(mult_Lo), .Hi(mult_Hi));
  Comparator #(.width(32), .mode("unsigned")) comparator_1 (.a(A), .b(B), .lt(comparator_1_lt));  // open: gt, eq
  assign sltu = {{31{1'b0}}, comparator_1_lt};  // Bit_Extender bit_extender_1
  Comparator #(.width(32)) comparator_2 (.a(A), .b(B), .lt(comparator_2_lt));  // open: gt, eq
  assign slt = {{31{1'b0}}, comparator_2_lt};  // Bit_Extender bit_extender_2
  Divider #(.width(32)) divider_1 (.a(A), .b(B), .out(divu_Lo), .rem(divu_Hi));  // open: upper
  Signed_Division signed_division_1 (.A(A), .B(B), .Lo(div_Lo), .Hi(div_Hi));
  Multiplexer #(.select(3), .width(32), .enable("false")) multiplexer_1 (
    .in0(add), .in1(sub), .in2(\or ), .in3(\nor ), .in4(\xor ), .in5(\and ), .in6(slt), .in7(sltu),
    .out(Result), .sel(Op));
  Multiplexer #(.select(2), .width(32), .enable("false")) multiplexer_2 (
    .in0(mult_Lo), .in1(mulu_Lo), .in2(div_Lo), .in3(divu_Lo), .out(Lo), .sel(Op[1:0]));
  Multiplexer #(.select(2), .width(32), .enable("false")) multiplexer_3 (
    .in0(mult_Hi), .in1(mulu_Hi), .in2(div_Hi), .in3(divu_Hi), .out(Hi), .sel(Op[1:0]));
  Comparator #(.width(32)) comparator_3 (.a(Result), .b({32{1'b0}}), .eq(Zero), .lt(Negative));  // open: gt

  // Other names for the same wires on the sheet: Mul_Div[1:0] = Op[1:0]

  // Notes on the sheet:
  //   000=add
  //   001=sub
  //   010=or
  //   011=nor
  //   100=xor
  //   101=and
  //   110=slt
  //   111=sltu
  //   Los Op son los sigientes:
  //   Unsigned
  //   Signed
  //   00=mul
  //   01=mulu
  //   10=div
  //   11=divu
  //   Esto se puede hacer por la forma en que esta construido el RF
  //   Los Op de la division y la multiplicacion son:
endmodule

module Signed_Multiplication (
  input  [31:0] A,
  input  [31:0] B,
  output [31:0] Lo,
  output [31:0] Hi
);

  wire A_Sign, adder_1_cout, B_Sign, Result_Sign;
  wire [31:0] denier_1_x_2, denier_2_x_2, minus_Hi, minus_Lo, not_1_out, not_2_out, plus_Hi, plus_Lo;

  Denier denier_1 (.X(A), .Negative(A_Sign), .x_2(denier_1_x_2));
  Denier denier_2 (.X(B), .Negative(B_Sign), .x_2(denier_2_x_2));
  xor xor_1 (Result_Sign, A_Sign, B_Sign);
  Multiplier #(.width(32)) multiplier_1 (
    .a(denier_1_x_2), .b(denier_2_x_2), .out(plus_Lo), .cout(plus_Hi));  // open: cin
  assign not_1_out = ~plus_Lo;  // NOT_Gate not_1, 32 bits wide
  assign not_2_out = ~plus_Hi;  // NOT_Gate not_2, 32 bits wide
  Adder #(.width(32)) adder_1 (.a(not_1_out), .b(32'h1), .out(minus_Lo), .cout(adder_1_cout));  // open: cin
  Adder #(.width(32)) adder_2 (.a(not_2_out), .b({32{1'b0}}), .out(minus_Hi), .cin(adder_1_cout));  // open: cout
  Multiplexer #(.width(32), .enable("false")) multiplexer_1 (
    .in0(plus_Lo), .in1(minus_Lo), .out(Lo), .sel(Result_Sign));
  Multiplexer #(.width(32), .enable("false")) multiplexer_2 (
    .in0(plus_Hi), .in1(minus_Hi), .out(Hi), .sel(Result_Sign));
endmodule

module Signed_Division (
  input  [31:0] A,
  input  [31:0] B,
  output [31:0] Lo,
  output [31:0] Hi
);

  wire A_Sign, B_Sign;
  wire [31:0] A__B__Q, A__B__Q_t, A__B__R, A__B__R_t, denier_1_x_2, denier_2_x_2, negator_2_out,
       plus_Quotient, plus_Rest, signed_multiplication_1_lo, signed_multiplication_2_lo;

  Denier denier_1 (.X(A), .Negative(A_Sign), .x_2(denier_1_x_2));
  Denier denier_2 (.X(B), .Negative(B_Sign), .x_2(denier_2_x_2));
  Adder #(.width(32)) adder_1 (.a(plus_Quotient), .b(32'h1), .out(A__B__Q_t));  // open: cin, cout
  Divider #(.width(32)) divider_1 (
    .a(denier_1_x_2), .b(denier_2_x_2), .out(plus_Quotient), .rem(plus_Rest));  // open: upper
  Negator #(.width(32)) negator_1 (.in(A__B__Q_t), .out(A__B__Q));
  Signed_Multiplication signed_multiplication_1 (.A(A__B__Q), .B(B), .Lo(signed_multiplication_1_lo));  // open: Hi
  Signed_Multiplication signed_multiplication_2 (.A(A__B__Q_t), .B(B), .Lo(signed_multiplication_2_lo));  // open: Hi
  Subtractor #(.width(32)) subtractor_1 (.a(A), .b(signed_multiplication_1_lo), .out(A__B__R));  // open: bin, bout
  Subtractor #(.width(32)) subtractor_2 (.a(A), .b(signed_multiplication_2_lo), .out(A__B__R_t));  // open: bin, bout
  Negator #(.width(32)) negator_2 (.in(plus_Quotient), .out(negator_2_out));
  // Probe on Lo
  Multiplexer #(.select(2), .width(32), .enable("false")) multiplexer_1 (
    .in0(plus_Quotient), .in1(negator_2_out), .in2(A__B__Q), .in3(A__B__Q_t), .out(Lo), .sel({A_Sign, B_Sign}));
  Multiplexer #(.select(2), .width(32), .enable("false")) multiplexer_2 (
    .in0(plus_Rest), .in1(plus_Rest), .in2(A__B__R), .in3(A__B__R_t), .out(Hi), .sel({A_Sign, B_Sign}));
  // Probe on Hi

  // Other names for the same wires on the sheet: Selector[1:0] = {A_Sign, B_Sign}
endmodule

module Denier (
  input  [31:0] X,
  output [31:0] x_2,
  output Negative
);

  wire [31:0] negator_1_out;

  Multiplexer #(.width(32), .enable("false")) multiplexer_1 (.in0(X), .in1(negator_1_out), .out(x_2), .sel(X[31]));
  Negator #(.width(32)) negator_1 (.in(X), .out(negator_1_out));

  assign Negative = X[31];
endmodule

module Instruction_Splitter (
  input  [31:0] Instruction,
  input  Clk,
  input  Reset,
  input  Instruction_Memory_R_W,
  output [5:0] OpCode,
  output [4:0] Rs,
  output [4:0] Rt,
  output [4:0] Rd,
  output [5:0] FuncCode,
  output [31:0] Unsigned_Const,
  output [31:0] Signed_Const,
  output [25:0] Jump_Target
);

  Register #(.width(32)) Instruction_Memory (
    .D(Instruction), .en(Instruction_Memory_R_W), .Q({OpCode, Jump_Target[25:6], FuncCode}), .clk(Clk),
    .clr(Reset));
  assign Unsigned_Const = {{16{1'b0}}, {Jump_Target[15:6], FuncCode}};  // Bit_Extender bit_extender_1
  assign Signed_Const = {{16{Jump_Target[15]}}, {Jump_Target[15:6], FuncCode}};  // Bit_Extender bit_extender_2

  assign Jump_Target[5:0] = FuncCode;
  assign Rd = Jump_Target[15:11];
  assign Rs = Jump_Target[25:21];
  assign Rt = Jump_Target[20:16];

  // Other names for the same wires on the sheet: In[31:0] = Instruction; Const[15:0] = {Jump_Target[15:6], FuncCode};
  //   Func_Code[5:0] = FuncCode; Out[31:0] = {OpCode, Jump_Target[25:6], FuncCode};
  //   Target[25:0] = {Jump_Target[25:6], FuncCode}; Op_Code[5:0] = OpCode; Rst = Reset; W_R = Instruction_Memory_R_W

  // Notes on the sheet:
  //   Inputs
  //   Split Instructions
  //   Outputs
endmodule

module Branch_Control (
  input  [31:0] PC,
  input  [25:0] Target,
  input  [31:0] Const,
  input  [31:0] Register_Value,
  input  [1:0] Branch_Type_Selector,
  input  [2:0] Flag_Selector,
  input  Zero_Flag,
  input  Negative_Flag,
  output [31:0] PC_prime
);

  wire Flag, gtz, lez, ne;
  wire [31:0] Increment, offset_4, PC_4, PC_4_offset_4;

  and and_1 (gtz, ~Zero_Flag, ~Negative_Flag);  // AND_Gate
  Multiplexer #(.select(3)) multiplexer_1 (
    .in0(Zero_Flag), .in1(ne), .in2(lez), .in3(gtz), .in4(Negative_Flag), .out(Flag), .sel(Flag_Selector));  // open: in5, in6, in7, en
  not not_1 (ne, Zero_Flag);
  or or_1 (lez, Zero_Flag, Negative_Flag);
  Shifter #(.width(32)) shifter_1 (.in(Const), .\dist (5'b00010), .out(offset_4));
  Adder #(.width(32)) adder_1 (.a(PC), .b(32'h4), .out(PC_4));  // open: cin, cout
  Adder #(.width(32)) adder_2 (.a(offset_4), .b(PC_4), .out(PC_4_offset_4));  // open: cin, cout
  Multiplexer #(.select(2), .width(32)) multiplexer_2 (
    .in0(PC_4), .in1(Register_Value), .in2({PC[31:28], Target, 2'b00}), .in3(Increment), .out(PC_prime),
    .sel(Branch_Type_Selector));  // open: en
  Multiplexer #(.width(32)) multiplexer_3 (.in0(PC_4), .in1(PC_4_offset_4), .out(Increment), .sel(Flag));  // open: en

  // Other names for the same wires on the sheet: BTS[1:0] = Branch_Type_Selector; eq = Zero_Flag; Z = Zero_Flag;
  //   FS[2:0] = Flag_Selector; Jump[31:2] = {PC[31:28], Target}; ltz = Negative_Flag; N = Negative_Flag;
  //   Reg[31:0] = Register_Value

  // Notes on the sheet:
  //   Inputs
  //   Branch Selector
  //   Branches
  //   PC Increment
  //   PC' Selector
  //   Increment Selector
  //   Output
endmodule

module Cache (
  input  IorD,
  input  Clk,
  input  [3:0] Read_Time,
  input  Rst,
  input  [3:0] Write_Time,
  input  start,
  input  nR_W_Ram,
  input  [31:0] Adr,
  input  [31:0] In0,
  input  [31:0] In1,
  input  [31:0] In2,
  input  [31:0] In3,
  input  [31:0] Data_Path,
  output [31:0] RAM_Out,
  output [15:0] Address,
  output Hit_Instruction,
  output Hit_Data,
  output CS,
  output [31:0] Out0,
  output RW,
  output [31:0] Out1,
  output [31:0] Out2,
  output [31:0] Out3,
  output [3:0] Mask
);

  wire data_cache_1_cs, Hit, instruction_cache_1_cs, StartD, StartI, Updt;
  wire [12:0] IT;
  wire [15:0] AddressD, AddressI;
  wire [31:0] Data, Instruction;

  Demultiplexer demultiplexer_1 (.out0(StartI), .out1(StartD), .in(start), .sel(IorD));  // open: en
  Multiplexer #(.width(32)) multiplexer_1 (.in0(Instruction), .in1(Data), .out(RAM_Out), .sel(IorD));  // open: en
  Multiplexer multiplexer_2 (.in0(Hit_Instruction), .in1(Hit_Data), .out(Hit), .sel(IorD));  // open: en
  Multiplexer #(.width(16)) multiplexer_3 (.in0(AddressI), .in1(AddressD), .out(Address), .sel(IorD));  // open: en
  Instruction_Cache instruction_cache_1 (
    .Clk(Clk), .Rst(Rst), .start(StartI), .Instruction(Instruction), .Read_Time(Read_Time),
    .Address(AddressI), .Adr(Adr), .Hit(Hit_Instruction), .In0(In0), .In1(In1), .In2(In2), .In3(In3),
    .CS(instruction_cache_1_cs), .Inst_Tag(IT), .New_Value(Data_Path), .Updt(Updt));
  Data_Cache data_cache_1 (
    .Clk(Clk), .Read_Time(Read_Time), .Data(Data), .Rst(Rst), .Write_Time(Write_Time), .Start(StartD),
    .Address(AddressD), .nR_W_Ram(nR_W_Ram), .Hit(Hit_Data), .Out0(Out0), .Adr(Adr), .Out1(Out1), .In0(In0),
    .Out2(Out2), .In1(In1), .Out3(Out3), .In2(In2), .In3(In3), .Data_Path(Data_Path), .Mask(Mask), .RW(RW),
    .CS(data_cache_1_cs), .Inst_Tag(IT), .Clear_Instruction(Updt));
  or or_1 (CS, instruction_cache_1_cs, data_cache_1_cs);

  // Other names for the same wires on the sheet: HitD = Hit_Data; HitI = Hit_Instruction; InDP[31:0] = Data_Path;
  //   Info[31:0] = RAM_Out; nRW = nR_W_Ram; RT[3:0] = Read_Time; WT[3:0] = Write_Time
endmodule

module Cache_Bank (
  input  [1:0] Block_OffSet,
  input  [12:0] TAG,
  input  [31:0] I0,
  input  [31:0] I1,
  input  [31:0] I2,
  input  [31:0] I3,
  input  [31:0] DP,
  input  Clk,
  input  Rst,
  input  Enable,
  input  Validate,
  input  Write,
  output [31:0] Data,
  output [12:0] Tag_2,
  output Validate_2
);

  wire or_1_out, or_2_out, or_3_out, or_4_out, W0, W1, W2, W3;
  wire [31:0] B0, B1, B2, B3, D0, D1, D2, D3, multiplexer_2_out, multiplexer_3_out, multiplexer_4_out,
       multiplexer_5_out;

  Register #(.width(13)) u_TAG (.D(TAG), .en(Enable), .Q(Tag_2), .clk(Clk), .clr(Rst));
  D_Flip_Flop u_Validate (.clk(Clk), .D(Validate), .Q(Validate_2), .en(Enable), .reset(Rst));  // open: Qn, preset
  Multiplexer #(.select(2), .width(32)) multiplexer_1 (
    .in0(B0), .in1(B1), .in2(B2), .in3(B3), .out(Data), .sel(Block_OffSet));  // open: en
  Demultiplexer #(.select(2), .width(32)) demultiplexer_1 (
    .out0(D0), .out1(D1), .out2(D2), .out3(D3), .in(DP), .sel(Block_OffSet));  // open: en
  Demultiplexer #(.select(2)) demultiplexer_2 (
    .out0(W0), .out1(W1), .out2(W2), .out3(W3), .in(Write), .sel(Block_OffSet));  // open: en
  Multiplexer #(.width(32)) multiplexer_2 (.in0(I0), .in1(D0), .out(multiplexer_2_out), .sel(Write));  // open: en
  Multiplexer #(.width(32)) multiplexer_3 (.in0(I2), .in1(D2), .out(multiplexer_3_out), .sel(Write));  // open: en
  Register #(.width(32)) u_B0 (.D(multiplexer_2_out), .en(or_1_out), .Q(B0), .clk(Clk), .clr(Rst));
  or or_1 (or_1_out, Enable, W0);
  Register #(.width(32)) u_B2 (.D(multiplexer_3_out), .en(or_2_out), .Q(B2), .clk(Clk), .clr(Rst));
  or or_2 (or_2_out, Enable, W2);
  Multiplexer #(.width(32)) multiplexer_4 (.in0(I1), .in1(D1), .out(multiplexer_4_out), .sel(Write));  // open: en
  or or_3 (or_3_out, Enable, W1);
  Multiplexer #(.width(32)) multiplexer_5 (.in0(I3), .in1(D3), .out(multiplexer_5_out), .sel(Write));  // open: en
  or or_4 (or_4_out, Enable, W3);
  Register #(.width(32)) u_B1 (.D(multiplexer_4_out), .en(or_3_out), .Q(B1), .clk(Clk), .clr(Rst));
  Register #(.width(32)) u_B3 (.D(multiplexer_5_out), .en(or_4_out), .Q(B3), .clk(Clk), .clr(Rst));

  // Other names for the same wires on the sheet: En = Enable; OffSet[1:0] = Block_OffSet; Tag_Out[12:0] = Tag_2;
  //   V = Validate_2; W = Write
endmodule

module Instruction_Cache (
  input  Clk,
  input  Rst,
  input  start,
  input  Updt,
  input  [3:0] Read_Time,
  input  [31:0] Adr,
  input  [31:0] In0,
  input  [31:0] In1,
  input  [31:0] In2,
  input  [31:0] In3,
  input  [31:0] New_Value,
  output [31:0] Instruction,
  output [15:0] Address,
  output Hit,
  output CS,
  output [12:0] Inst_Tag
);

  wire and_2_out, comparator_1_eq, comparator_2_lt, d_ff_1_q, demultiplexer_3_out0, E0, E1, E2, E3, E4, E5,
       E6, E7, Loaded, or_2_out, RT_Ready, V0, V1, V2, V3, V4, V5, V6, V7, Valid, W0, W1, W2, W3, W4, W5, W6,
       W7;
  wire [3:0] counter_1_q;
  wire [12:0] TC0, TC1, TC2, TC3, TC4, TC5, TC6, TC7;
  wire [31:0] D0, D1, D2, D3, D4, D5, D6, D7;

  Demultiplexer #(.select(3)) demultiplexer_1 (
    .out0(E0), .out1(E1), .out2(E2), .out3(E3), .out4(E4), .out5(E5), .out6(E6), .out7(E7), .in(RT_Ready),
    .sel(Adr[6:4]));  // open: en
  Cache_Bank cache_bank_1 (
    .Block_OffSet(Adr[3:2]), .Data(D0), .TAG(Adr[19:7]), .Tag_2(TC0), .I0(In0), .Validate_2(V0), .I1(In1),
    .I2(In2), .I3(In3), .DP(New_Value), .Clk(Clk), .Rst(Rst), .Enable(E0), .Validate(RT_Ready), .Write(W0));
  Cache_Bank cache_bank_2 (
    .Block_OffSet(Adr[3:2]), .Data(D3), .TAG(Adr[19:7]), .Tag_2(TC3), .I0(In0), .Validate_2(V3), .I1(In1),
    .I2(In2), .I3(In3), .DP(New_Value), .Clk(Clk), .Rst(Rst), .Enable(E3), .Validate(RT_Ready), .Write(W3));
  Cache_Bank cache_bank_3 (
    .Block_OffSet(Adr[3:2]), .Data(D6), .TAG(Adr[19:7]), .Tag_2(TC6), .I0(In0), .Validate_2(V6), .I1(In1),
    .I2(In2), .I3(In3), .DP(New_Value), .Clk(Clk), .Rst(Rst), .Enable(E6), .Validate(RT_Ready), .Write(W6));
  Multiplexer #(.select(3), .width(32)) multiplexer_1 (
    .in0(D0), .in1(D1), .in2(D2), .in3(D3), .in4(D4), .in5(D5), .in6(D6), .in7(D7),
    .out({Instruction[7:0], Instruction[15:8], Instruction[23:16], Instruction[31:24]}), .sel(Adr[6:4]));  // open: en
  Comparator #(.width(13)) comparator_1 (.a(Inst_Tag), .b(Adr[19:7]), .eq(comparator_1_eq));  // open: gt, lt
  Demultiplexer #(.select(3)) demultiplexer_2 (
    .out0(W0), .out1(W1), .out2(W2), .out3(W3), .out4(W4), .out5(W5), .out6(W6), .out7(W7), .in(Updt),
    .sel(Adr[6:4]));  // open: en
  and and_1 (Hit, comparator_1_eq, Valid);
  Cache_Bank cache_bank_4 (
    .Block_OffSet(Adr[3:2]), .Data(D1), .TAG(Adr[19:7]), .Tag_2(TC1), .I0(In0), .Validate_2(V1), .I1(In1),
    .I2(In2), .I3(In3), .DP(New_Value), .Clk(Clk), .Rst(Rst), .Enable(E1), .Validate(RT_Ready), .Write(W1));
  Cache_Bank cache_bank_5 (
    .Block_OffSet(Adr[3:2]), .Data(D4), .TAG(Adr[19:7]), .Tag_2(TC4), .I0(In0), .Validate_2(V4), .I1(In1),
    .I2(In2), .I3(In3), .DP(New_Value), .Clk(Clk), .Rst(Rst), .Enable(E4), .Validate(RT_Ready), .Write(W4));
  Cache_Bank cache_bank_6 (
    .Block_OffSet(Adr[3:2]), .Data(D7), .TAG(Adr[19:7]), .Tag_2(TC7), .I0(In0), .Validate_2(V7), .I1(In1),
    .I2(In2), .I3(In3), .DP(New_Value), .Clk(Clk), .Rst(Rst), .Enable(E7), .Validate(RT_Ready), .Write(W7));
  Multiplexer #(.select(3), .width(13)) multiplexer_2 (
    .in0(TC0), .in1(TC1), .in2(TC2), .in3(TC3), .in4(TC4), .in5(TC5), .in6(TC6), .in7(TC7), .out(Inst_Tag),
    .sel(Adr[6:4]));  // open: en
  Multiplexer #(.select(3)) multiplexer_3 (
    .in0(V0), .in1(V1), .in2(V2), .in3(V3), .in4(V4), .in5(V5), .in6(V6), .in7(V7), .out(Valid),
    .sel(Adr[6:4]));  // open: en
  Cache_Bank cache_bank_7 (
    .Block_OffSet(Adr[3:2]), .Data(D2), .TAG(Adr[19:7]), .Tag_2(TC2), .I0(In0), .Validate_2(V2), .I1(In1),
    .I2(In2), .I3(In3), .DP(New_Value), .Clk(Clk), .Rst(Rst), .Enable(E2), .Validate(RT_Ready), .Write(W2));
  Cache_Bank cache_bank_8 (
    .Block_OffSet(Adr[3:2]), .Data(D5), .TAG(Adr[19:7]), .Tag_2(TC5), .I0(In0), .Validate_2(V5), .I1(In1),
    .I2(In2), .I3(In3), .DP(New_Value), .Clk(Clk), .Rst(Rst), .Enable(E5), .Validate(RT_Ready), .Write(W5));
  D_Flip_Flop d_ff_1 (.clk(Clk), .D(demultiplexer_3_out0), .Q(d_ff_1_q));  // open: Qn, preset, en, reset
  and and_2 (and_2_out, start, ~Hit);  // AND_Gate
  or or_1 (CS, d_ff_1_q, and_2_out);
  Counter #(.width(4), .max('hf)) counter_1 (
    .count(CS), .Q(counter_1_q), .clk(Clk), .clr(or_2_out));  // open: load, D, carry
  or or_2 (or_2_out, Rst, Hit);
  Demultiplexer demultiplexer_3 (.out0(demultiplexer_3_out0), .out1(RT_Ready), .in(CS), .sel(Loaded));  // open: en
  Comparator #(.width(4)) comparator_2 (.a(counter_1_q), .b(Read_Time), .lt(comparator_2_lt));  // open: gt, eq
  not not_1 (Loaded, comparator_2_lt);

  assign Address = Adr[19:4];

  // Other names for the same wires on the sheet: OffSet[1:0] = Adr[3:2]; Index[2:0] = Adr[6:4]; Tag[12:0] = Adr[19:7];
  //   Counter = CS; New[31:0] = New_Value; RT[3:0] = Read_Time; Tag_Copy[12:0] = Inst_Tag; Validated = RT_Ready
endmodule

module Data_Cache (
  input  [3:0] Read_Time,
  input  Rst,
  input  [3:0] Write_Time,
  input  Start,
  input  nR_W_Ram,
  input  [31:0] Adr,
  input  [31:0] In0,
  input  [31:0] In1,
  input  [31:0] In2,
  input  [31:0] In3,
  input  [31:0] Data_Path,
  input  Clk,
  input  [12:0] Inst_Tag,
  output [31:0] Data,
  output [15:0] Address,
  output Hit,
  output [31:0] Out0,
  output [31:0] Out1,
  output [31:0] Out2,
  output [31:0] Out3,
  output [3:0] Mask,
  output RW,
  output Clear_Instruction,
  output CS
);

  wire and_3_out, comparator_1_eq, comparator_2_eq, comparator_3_lt, d_ff_1_q, demultiplexer_4_out0,
       demultiplexer_4_out1, demultiplexer_5_out1, E0, E1, E2, E3, E4, E5, E6, E7, Hit1, Hit2, Loaded,
       or_2_out, RT_Ready, V0, V1, V2, V3, V4, V5, V6, V7, Valid, W0, W1, W2, W3, W4, W5, W6, W7, Write;
  wire [3:0] counter_1_q, T;
  wire [12:0] Tag_Copy, TC0, TC1, TC2, TC3, TC4, TC5, TC6, TC7;
  wire [31:0] D0, D1, D2, D3, D4, D5, D6, D7;

  Decoder #(.select(2)) decoder_1 (
    .out0(Mask[0]), .out1(Mask[1]), .out2(Mask[2]), .out3(Mask[3]), .sel(Adr[3:2]));  // open: en
  Demultiplexer #(.select(3)) demultiplexer_1 (
    .out0(E0), .out1(E1), .out2(E2), .out3(E3), .out4(E4), .out5(E5), .out6(E6), .out7(E7), .in(RT_Ready),
    .sel(Adr[6:4]));  // open: en
  Cache_Bank cache_bank_1 (
    .Block_OffSet(Adr[3:2]), .Data(D0), .TAG(Adr[19:7]), .Tag_2(TC0), .I0(In0), .Validate_2(V0), .I1(In1),
    .I2(In2), .I3(In3), .DP(Data_Path), .Clk(Clk), .Rst(Rst), .Enable(E0), .Validate(RT_Ready), .Write(W0));
  Cache_Bank cache_bank_2 (
    .Block_OffSet(Adr[3:2]), .Data(D3), .TAG(Adr[19:7]), .Tag_2(TC3), .I0(In0), .Validate_2(V3), .I1(In1),
    .I2(In2), .I3(In3), .DP(Data_Path), .Clk(Clk), .Rst(Rst), .Enable(E3), .Validate(RT_Ready), .Write(W3));
  Cache_Bank cache_bank_3 (
    .Block_OffSet(Adr[3:2]), .Data(D6), .TAG(Adr[19:7]), .Tag_2(TC6), .I0(In0), .Validate_2(V6), .I1(In1),
    .I2(In2), .I3(In3), .DP(Data_Path), .Clk(Clk), .Rst(Rst), .Enable(E6), .Validate(RT_Ready), .Write(W6));
  Multiplexer #(.select(3), .width(32)) multiplexer_1 (
    .in0(D0), .in1(D1), .in2(D2), .in3(D3), .in4(D4), .in5(D5), .in6(D6), .in7(D7),
    .out({Data[7:0], Data[15:8], Data[23:16], Data[31:24]}), .sel(Adr[6:4]));  // open: en
  Comparator #(.width(13)) comparator_1 (.a(Tag_Copy), .b(Adr[19:7]), .eq(comparator_1_eq));  // open: gt, lt
  Comparator #(.width(13)) comparator_2 (.a(Adr[19:7]), .b(Inst_Tag), .eq(comparator_2_eq));  // open: gt, lt
  Demultiplexer #(.select(3)) demultiplexer_2 (
    .out0(W0), .out1(W1), .out2(W2), .out3(W3), .out4(W4), .out5(W5), .out6(W6), .out7(W7), .in(Write),
    .sel(Adr[6:4]));  // open: en
  and and_1 (Hit1, comparator_1_eq, Valid);
  and and_2 (Clear_Instruction, comparator_2_eq, Hit2);
  Demultiplexer #(.select(2), .width(32)) demultiplexer_3 (
    .out0(Out0), .out1(Out1), .out2(Out2), .out3(Out3),
    .in({Data_Path[7:0], Data_Path[15:8], Data_Path[23:16], Data_Path[31:24]}), .sel(Adr[3:2]));  // open: en
  Cache_Bank cache_bank_4 (
    .Block_OffSet(Adr[3:2]), .Data(D1), .TAG(Adr[19:7]), .Tag_2(TC1), .I0(In0), .Validate_2(V1), .I1(In1),
    .I2(In2), .I3(In3), .DP(Data_Path), .Clk(Clk), .Rst(Rst), .Enable(E1), .Validate(RT_Ready), .Write(W1));
  Cache_Bank cache_bank_5 (
    .Block_OffSet(Adr[3:2]), .Data(D4), .TAG(Adr[19:7]), .Tag_2(TC4), .I0(In0), .Validate_2(V4), .I1(In1),
    .I2(In2), .I3(In3), .DP(Data_Path), .Clk(Clk), .Rst(Rst), .Enable(E4), .Validate(RT_Ready), .Write(W4));
  Cache_Bank cache_bank_6 (
    .Block_OffSet(Adr[3:2]), .Data(D7), .TAG(Adr[19:7]), .Tag_2(TC7), .I0(In0), .Validate_2(V7), .I1(In1),
    .I2(In2), .I3(In3), .DP(Data_Path), .Clk(Clk), .Rst(Rst), .Enable(E7), .Validate(RT_Ready), .Write(W7));
  Multiplexer #(.select(3), .width(13)) multiplexer_2 (
    .in0(TC0), .in1(TC1), .in2(TC2), .in3(TC3), .in4(TC4), .in5(TC5), .in6(TC6), .in7(TC7), .out(Tag_Copy),
    .sel(Adr[6:4]));  // open: en
  Multiplexer #(.select(3)) multiplexer_3 (
    .in0(V0), .in1(V1), .in2(V2), .in3(V3), .in4(V4), .in5(V5), .in6(V6), .in7(V7), .out(Valid),
    .sel(Adr[6:4]));  // open: en
  D_Flip_Flop d_ff_1 (.clk(Clk), .D(demultiplexer_4_out0), .Q(d_ff_1_q), .reset(Rst));  // open: Qn, preset, en
  and and_3 (and_3_out, Start, ~Hit);  // AND_Gate
  Cache_Bank cache_bank_7 (
    .Block_OffSet(Adr[3:2]), .Data(D2), .TAG(Adr[19:7]), .Tag_2(TC2), .I0(In0), .Validate_2(V2), .I1(In1),
    .I2(In2), .I3(In3), .DP(Data_Path), .Clk(Clk), .Rst(Rst), .Enable(E2), .Validate(RT_Ready), .Write(W2));
  Cache_Bank cache_bank_8 (
    .Block_OffSet(Adr[3:2]), .Data(D5), .TAG(Adr[19:7]), .Tag_2(TC5), .I0(In0), .Validate_2(V5), .I1(In1),
    .I2(In2), .I3(In3), .DP(Data_Path), .Clk(Clk), .Rst(Rst), .Enable(E5), .Validate(RT_Ready), .Write(W5));
  or or_1 (CS, d_ff_1_q, and_3_out);
  Counter #(.width(4), .max('hf)) counter_1 (
    .count(CS), .Q(counter_1_q), .clk(Clk), .clr(or_2_out));  // open: load, D, carry
  or or_2 (or_2_out, Rst, Hit);
  Multiplexer multiplexer_4 (.in0(Hit1), .in1(Hit2), .out(Hit), .sel(nR_W_Ram));  // open: en
  Multiplexer #(.width(4)) multiplexer_5 (.in0(Read_Time), .in1(Write_Time), .out(T), .sel(nR_W_Ram));  // open: en
  Demultiplexer demultiplexer_4 (
    .out0(demultiplexer_4_out0), .out1(demultiplexer_4_out1), .in(CS), .sel(Loaded));  // open: en
  Comparator #(.width(4)) comparator_3 (.a(counter_1_q), .b(T), .lt(comparator_3_lt));  // open: gt, eq
  not not_1 (Loaded, comparator_3_lt);
  Demultiplexer demultiplexer_5 (
    .out0(RT_Ready), .out1(demultiplexer_5_out1), .in(demultiplexer_4_out1), .sel(nR_W_Ram));  // open: en
  and and_4 (RW, nR_W_Ram, CS);
  D_Flip_Flop d_ff_2 (.clk(Clk), .D(demultiplexer_5_out1), .Q(Hit2), .reset(Rst));  // open: Qn, preset, en
  and and_5 (Write, Hit2, Hit1);

  assign Address = Adr[19:4];

  // Other names for the same wires on the sheet: InDP[31:0] = Data_Path; OffSet[1:0] = Adr[3:2];
  //   Index[2:0] = Adr[6:4]; Tag[12:0] = Adr[19:7]; RT[3:0] = Read_Time; RW_t = nR_W_Ram; Validated = RT_Ready;
  //   Counter = CS; W_Ram = CS; WT[3:0] = Write_Time; WT_Ready = Hit2
endmodule

module Control_Unit_2 (
  input  [5:0] OpCode,
  input  [5:0] FuncCode,
  input  rst,
  input  Clock,
  input  in_5,
  input  in_6,
  output [2:0] out_7,
  output [2:0] out_8,
  output [1:0] out_9,
  output [1:0] out_10,
  output out_11,
  output out_12,
  output [2:0] out_13,
  output out_14,
  output [1:0] out_15,
  output out_16,
  output out_17,
  output out_18,
  output out_19,
  output out_20,
  output out_21,
  output out_22,
  output out_23,
  output out_24
);

  wire add, addi, \and , andi, beq, bgtz, blez, bltz, bne, d_ff_1_q, d_ff_2_q, demultiplexer_1_out0,
       demultiplexer_1_out1, demultiplexer_2_out0, div, divu, En_AL, En_B, En_I, En_S, En_Sp, En_W, EndS,
       Endw, haltl, jmp, jr, kbd_t, Load_IM_q, lw, mfhi, mflo, mul, mulu, nop, \nor , \or , or_1_out,
       or_3_out, ori, PCal, PCb, PCi, PCs, PCsp, PCw, pop, push, RamWs, RamWw, RFal, RfE, RFi, Rfs, Rfw, rnd,
       S_As, S_DAi, S_DAw, slt, slti, sltiu, sltu, start, StartRamF, StartRams, StartRamw, sub, sw, tty_t,
       Type_AL, Type_B, Type_I, Type_S, Type_Sp, Type_W, \xor , xori;
  wire [1:0] or_14_out, or_18_out, S_Adrs, S_Adrw, S_BCal, S_BCb, S_Bi, S_Bs, S_Bw;
  wire [2:0] S_ALUal, S_ALUb, S_ALUi, S_ALUs, S_Dial, S_DiE, S_Dis, S_Diw;

  not not_1 (start, rst);
  Main_Decoder Main_Decoder (
    .OpCode(OpCode), .FuncCode(FuncCode), .addi(addi), .beq(beq), .slti(slti), .add(add), .\and (\and ),
    .nop(nop), .andi(andi), .bne(bne), .sltiu(sltiu), .ori(ori), .blez(blez), .lw(lw), .sub(sub),
    .\or (\or ), .push(push), .xori(xori), .bgtz(bgtz), .sw(sw), .pop(pop), .mul(mul), .\nor (\nor ),
    .jmp(jmp), .bltz(bltz), .tty(tty_t), .mulu(mulu), .\xor (\xor ), .div(div), .mfhi(mfhi), .halt(haltl),
    .mflo(mflo), .divu(divu), .rnd(rnd), .slt(slt), .jr(jr), .kbd(kbd_t), .sltu(sltu));
  D_Flip_Flop d_ff_1 (.clk(Clock), .D(demultiplexer_1_out0), .Q(d_ff_1_q), .preset(rst));  // open: Qn, en, reset
  Demultiplexer #(.enable("false")) demultiplexer_1 (
    .out0(demultiplexer_1_out0), .out1(demultiplexer_1_out1), .in(or_1_out), .sel(start));
  or or_1 (or_1_out, d_ff_1_q, out_20);
  D_Flip_Flop d_ff_2 (.clk(Clock), .D(StartRamF), .Q(d_ff_2_q), .reset(rst));  // open: Qn, preset, en
  or or_2 (StartRamF, demultiplexer_1_out1, demultiplexer_2_out0);
  Demultiplexer #(.enable("false")) demultiplexer_2 (
    .out0(demultiplexer_2_out0), .out1(out_11), .in(d_ff_2_q), .sel(in_5));
  Type_Al_Decoder type_al_decoder_1 (
    .in_1(En_AL), .in_2(add), .in_3(sub), .in_4(\and ), .in_5(\or ), .in_6(\xor ), .in_7(\nor ), .in_8(slt),
    .in_9(sltu), .in_10(mul), .in_11(mulu), .in_12(div), .in_13(divu), .in_14(mfhi), .in_15(mflo),
    .in_16(jr), .in_17(nop), .out_19(RFal), .out_20(S_ALUal), .out_23(S_BCal), .out_21(out_17),
    .out_22(S_Dial), .out_18(PCal));
  D_Flip_Flop Load_IM (.clk(Clock), .D(out_11), .Q(Load_IM_q), .reset(rst));  // open: Qn, preset, en
  or or_3 (or_3_out, haltl, out_16);
  and and_1 (En_AL, Type_AL, Load_IM_q);
  and and_2 (En_I, Type_I, Load_IM_q);
  and and_3 (En_B, Type_B, Load_IM_q);
  and and_4 (En_W, Type_W, Load_IM_q);
  and and_5 (En_Sp, Type_Sp, Load_IM_q);
  and and_6 (En_S, Type_S, Load_IM_q);
  D_Flip_Flop Halt (.clk(Clock), .D(or_3_out), .Q(out_16), .reset(rst));  // open: Qn, preset, en
  Type_Inm_Decoder type_inm_decoder_1 (
    .in_1(En_I), .in_2(addi), .in_3(andi), .in_4(ori), .in_5(xori), .in_6(slti), .in_7(sltiu),
    .out_10(S_DAi), .out_11(PCi), .out_12(RFi), .out_9(S_Bi), .out_8(S_ALUi));
  Type_Stack type_stack_1 (
    .in_1(pop), .in_2(push), .in_3(En_S), .in_4(in_6), .in_6(Clock), .out_12(S_As), .out_15(S_Bs),
    .out_18(out_24), .out_10(S_Adrs), .out_13(PCs), .out_17(S_ALUs), .out_11(StartRams), .out_16(S_Dis),
    .out_14(EndS), .out_7(Rfs), .out_8(RamWs), .out_9(out_12), .Rst(rst));
  or or_4 (Type_B, beq, bne, blez, bgtz, bltz, jmp);
  or or_5 (Type_AL, add, sub, \and , \or , \xor , \nor , slt, sltu, mul, mulu, div, divu, mfhi, mflo, jr, nop);
  or or_6 (Type_W, lw, sw);
  or or_7 (Type_S, pop, push);
  Type_Branch type_branch_1 (
    .in_1(En_B), .in_2(beq), .in_3(bne), .in_4(blez), .in_5(bgtz), .in_6(bltz), .in_7(jmp), .out_8(PCb),
    .out_11(out_13), .out_9(S_ALUb), .out_10(S_BCb));
  or or_8 (Type_I, addi, andi, ori, xori, slti, sltiu);
  or or_9 (Type_Sp, kbd_t, rnd, tty_t);
  or or_10 (out_20, En_AL, En_I, En_Sp, En_B, Endw, EndS);
  Type_Word type_word_1 (
    .in_1(En_W), .in_2(Clock), .in_3(lw), .in_5(in_6), .in_6(sw), .out_14(S_Diw), .out_9(Endw),
    .out_10(StartRamw), .out_11(S_Bw), .out_13(S_Adrw), .out_15(PCw), .out_12(RamWw), .out_7(Rfw),
    .out_8(S_DAw), .Rst(rst));
  Type_Special type_special_1 (
    .in_1(En_Sp), .in_2(kbd_t), .in_3(rnd), .in_4(tty_t), .out_7(out_21), .out_5(RfE), .out_6(S_DiE),
    .out_8(PCsp), .out_9(out_23));
  Multiplexer #(.select(2), .width(3)) multiplexer_1 (
    .in0(S_ALUal), .in1(S_ALUi), .in2(S_ALUb), .in3(S_ALUs), .out(out_7), .sel(or_14_out));  // open: en
  or or_11 (or_14_out[1], Type_S, Type_B);
  Multiplexer #(.select(2), .width(2)) multiplexer_2 (
    .in0(S_Bs), .in1(S_Bi), .in2(S_Bw), .out(out_9), .sel({Type_W, Type_I}));  // open: in3, en
  assign out_15 = S_BCb | S_BCal;  // OR_Gate or_12, 2 bits wide
  or or_13 (out_19, RamWs, RamWw);
  or or_14 (or_14_out[0], Type_I, Type_S);
  or or_15 (out_22, StartRams, StartRamF, StartRamw);
  Multiplexer #(.select(2), .width(3)) multiplexer_3 (
    .in0(S_Dial), .in1(S_Dis), .in2(S_Diw), .in3(S_DiE), .out(out_8), .sel(or_18_out));  // open: en
  or or_16 (or_18_out[1], Type_W, Type_Sp);
  Multiplexer #(.width(2)) multiplexer_4 (.in0(S_Adrs), .in1(S_Adrw), .out(out_10), .sel(Type_W));  // open: en
  Multiplexer multiplexer_5 (.in0(S_DAi), .in1(S_DAw), .out(out_14), .sel(Type_W));  // open: en
  or or_17 (out_18, RfE, RFal, RFi, Rfw, Rfs);
  or or_18 (or_18_out[0], Type_Sp, Type_S);

  // Other names for the same wires on the sheet: Clk = Clock; DataReady = in_6; HALT = out_16; En_KBD = out_23;
  //   KBD = out_23; L_IM = out_11; L_LoHi = out_17; LH = out_17; next = out_20; PC = out_20; RamReady = in_5;
  //   RamW = out_19; Rf_Rw = out_18; S_Adr[1:0] = out_10; S_ALU[2:0] = out_7; S_B[1:0] = out_9; S_BC[1:0] = out_15;
  //   S_DA = out_14; S_Di[2:0] = out_8; S_DO = out_12; S_flag[2:0] = out_13; S_flags[2:0] = out_13; SP = out_24;
  //   SPs = out_24; StartRam = out_22; TTY = out_21; tty_En = out_21
endmodule

module Main_Decoder (
  input  [5:0] OpCode,
  input  [5:0] FuncCode,
  output addi,
  output beq,
  output slti,
  output add,
  output \and ,
  output nop,
  output andi,
  output bne,
  output sltiu,
  output ori,
  output blez,
  output lw,
  output sub,
  output \or ,
  output push,
  output xori,
  output bgtz,
  output sw,
  output pop,
  output mul,
  output \nor ,
  output jmp,
  output bltz,
  output tty,
  output mulu,
  output \xor ,
  output div,
  output mfhi,
  output halt,
  output mflo,
  output divu,
  output rnd,
  output slt,
  output jr,
  output kbd,
  output sltu
);

  wire and_18_out, and_19_out, and_20_out, and_21_out, and_22_out, and_23_out, and_24_out, and_25_out,
       and_34_out, and_35_out, and_36_out, and_37_out, and_38_out, and_39_out, and_40_out, and_48_out,
       and_49_out, and_50_out, and_51_out, and_52_out, and_53_out, and_54_out, special, stack, Tipo_R;

  and and_1 (Tipo_R, ~OpCode[0], ~OpCode[1], ~OpCode[2], ~OpCode[3], ~OpCode[4], ~OpCode[5]);  // AND_Gate
  and and_2 (addi, ~OpCode[0], ~OpCode[1], ~OpCode[2], OpCode[3], ~OpCode[4], ~OpCode[5]);  // AND_Gate
  and and_3 (andi, ~OpCode[0], ~OpCode[1], OpCode[2], OpCode[3], ~OpCode[4], ~OpCode[5]);  // AND_Gate
  and and_4 (ori, OpCode[0], ~OpCode[1], OpCode[2], OpCode[3], ~OpCode[4], ~OpCode[5]);  // AND_Gate
  and and_5 (xori, ~OpCode[0], OpCode[1], OpCode[2], OpCode[3], ~OpCode[4], ~OpCode[5]);  // AND_Gate
  and and_6 (jmp, ~OpCode[0], OpCode[1], ~OpCode[2], ~OpCode[3], ~OpCode[4], ~OpCode[5]);  // AND_Gate
  and and_7 (stack, ~OpCode[0], ~OpCode[1], ~OpCode[2], OpCode[3], OpCode[4], OpCode[5]);  // AND_Gate
  and and_8 (beq, ~OpCode[0], ~OpCode[1], OpCode[2], ~OpCode[3], ~OpCode[4], ~OpCode[5]);  // AND_Gate
  and and_9 (bne, OpCode[0], ~OpCode[1], OpCode[2], ~OpCode[3], ~OpCode[4], ~OpCode[5]);  // AND_Gate
  and and_10 (blez, ~OpCode[0], OpCode[1], OpCode[2], ~OpCode[3], ~OpCode[4], ~OpCode[5]);  // AND_Gate
  and and_11 (bgtz, OpCode[0], OpCode[1], OpCode[2], ~OpCode[3], ~OpCode[4], ~OpCode[5]);  // AND_Gate
  and and_12 (bltz, OpCode[0], ~OpCode[1], ~OpCode[2], ~OpCode[3], ~OpCode[4], ~OpCode[5]);  // AND_Gate
  and and_13 (special, OpCode[0], OpCode[1], OpCode[2], OpCode[3], OpCode[4], OpCode[5]);
  and and_14 (slti, ~OpCode[0], OpCode[1], ~OpCode[2], OpCode[3], ~OpCode[4], ~OpCode[5]);  // AND_Gate
  and and_15 (sltiu, OpCode[0], OpCode[1], ~OpCode[2], OpCode[3], ~OpCode[4], ~OpCode[5]);  // AND_Gate
  and and_16 (lw, OpCode[0], OpCode[1], ~OpCode[2], ~OpCode[3], ~OpCode[4], OpCode[5]);  // AND_Gate
  and and_17 (sw, OpCode[0], OpCode[1], ~OpCode[2], OpCode[3], ~OpCode[4], OpCode[5]);  // AND_Gate
  and and_18 (and_18_out, ~FuncCode[0], ~FuncCode[1], ~FuncCode[2], ~FuncCode[3], ~FuncCode[4], FuncCode[5]);  // AND_Gate
  and and_19 (and_19_out, ~FuncCode[0], FuncCode[1], ~FuncCode[2], ~FuncCode[3], ~FuncCode[4], FuncCode[5]);  // AND_Gate
  and and_20 (and_20_out, ~FuncCode[0], ~FuncCode[1], ~FuncCode[2], FuncCode[3], FuncCode[4], ~FuncCode[5]);  // AND_Gate
  and and_21 (and_21_out, FuncCode[0], ~FuncCode[1], ~FuncCode[2], FuncCode[3], FuncCode[4], ~FuncCode[5]);  // AND_Gate
  and and_22 (and_22_out, ~FuncCode[0], FuncCode[1], ~FuncCode[2], FuncCode[3], FuncCode[4], ~FuncCode[5]);  // AND_Gate
  and and_23 (and_23_out, FuncCode[0], FuncCode[1], ~FuncCode[2], FuncCode[3], FuncCode[4], ~FuncCode[5]);  // AND_Gate
  and and_24 (and_24_out, ~FuncCode[0], FuncCode[1], ~FuncCode[2], FuncCode[3], ~FuncCode[4], FuncCode[5]);  // AND_Gate
  and and_25 (and_25_out, FuncCode[0], FuncCode[1], ~FuncCode[2], FuncCode[3], ~FuncCode[4], FuncCode[5]);  // AND_Gate
  and and_26 (add, and_18_out, Tipo_R);
  and and_27 (sub, and_19_out, Tipo_R);
  and and_28 (mul, and_20_out, Tipo_R);
  and and_29 (mulu, and_21_out, Tipo_R);
  and and_30 (div, and_22_out, Tipo_R);
  and and_31 (divu, and_23_out, Tipo_R);
  and and_32 (slt, and_24_out, Tipo_R);
  and and_33 (sltu, and_25_out, Tipo_R);
  and and_34 (and_34_out, ~FuncCode[0], ~FuncCode[1], FuncCode[2], ~FuncCode[3], ~FuncCode[4], FuncCode[5]);  // AND_Gate
  and and_35 (and_35_out, FuncCode[0], ~FuncCode[1], FuncCode[2], ~FuncCode[3], ~FuncCode[4], FuncCode[5]);  // AND_Gate
  and and_36 (and_36_out, FuncCode[0], FuncCode[1], FuncCode[2], ~FuncCode[3], ~FuncCode[4], FuncCode[5]);  // AND_Gate
  and and_37 (and_37_out, ~FuncCode[0], ~FuncCode[1], ~FuncCode[2], FuncCode[3], ~FuncCode[4], FuncCode[5]);  // AND_Gate
  and and_38 (and_38_out, ~FuncCode[0], ~FuncCode[1], ~FuncCode[2], ~FuncCode[3], FuncCode[4], ~FuncCode[5]);  // AND_Gate
  and and_39 (and_39_out, ~FuncCode[0], FuncCode[1], ~FuncCode[2], ~FuncCode[3], FuncCode[4], ~FuncCode[5]);  // AND_Gate
  and and_40 (and_40_out, ~FuncCode[0], ~FuncCode[1], ~FuncCode[2], FuncCode[3], ~FuncCode[4], ~FuncCode[5]);  // AND_Gate
  and and_41 (\and , and_34_out, Tipo_R);
  and and_42 (\or , and_35_out, Tipo_R);
  and and_43 (\nor , and_36_out, Tipo_R);
  and and_44 (\xor , and_37_out, Tipo_R);
  and and_45 (mfhi, and_38_out, Tipo_R);
  and and_46 (mflo, and_39_out, Tipo_R);
  and and_47 (jr, and_40_out, Tipo_R);
  and and_48 (and_48_out, ~FuncCode[0], ~FuncCode[1], ~FuncCode[2], ~FuncCode[3], ~FuncCode[4], ~FuncCode[5]);  // AND_Gate
  and and_49 (and_49_out, FuncCode[0], ~FuncCode[1], ~FuncCode[2], ~FuncCode[3], ~FuncCode[4], ~FuncCode[5]);  // AND_Gate
  and and_50 (and_50_out, ~FuncCode[0], ~FuncCode[1], ~FuncCode[2], ~FuncCode[3], ~FuncCode[4], ~FuncCode[5]);  // AND_Gate
  and and_51 (and_51_out, FuncCode[0], ~FuncCode[1], ~FuncCode[2], ~FuncCode[3], ~FuncCode[4], ~FuncCode[5]);  // AND_Gate
  and and_52 (and_52_out, FuncCode[0], FuncCode[1], FuncCode[2], FuncCode[3], FuncCode[4], FuncCode[5]);
  and and_53 (and_53_out, ~FuncCode[0], FuncCode[1], ~FuncCode[2], ~FuncCode[3], ~FuncCode[4], ~FuncCode[5]);  // AND_Gate
  and and_54 (and_54_out, ~FuncCode[0], ~FuncCode[1], FuncCode[2], ~FuncCode[3], ~FuncCode[4], ~FuncCode[5]);  // AND_Gate
  and and_55 (nop, and_48_out, Tipo_R);
  and and_56 (push, and_49_out, stack);
  and and_57 (pop, and_50_out, stack);
  and and_58 (tty, and_51_out, special);
  and and_59 (halt, and_52_out, special);
  and and_60 (rnd, and_53_out, special);
  and and_61 (kbd, and_54_out, special);

  // Other names for the same wires on the sheet: f0 = FuncCode[0]; f1 = FuncCode[1]; f2 = FuncCode[2];
  //   f3 = FuncCode[3]; f4 = FuncCode[4]; f5 = FuncCode[5]; o0 = OpCode[0]; o1 = OpCode[1]; o2 = OpCode[2];
  //   o3 = OpCode[3]; o4 = OpCode[4]; o5 = OpCode[5]
endmodule

module Type_Al_Decoder (
  input  in_1,
  input  in_2,
  input  in_3,
  input  in_4,
  input  in_5,
  input  in_6,
  input  in_7,
  input  in_8,
  input  in_9,
  input  in_10,
  input  in_11,
  input  in_12,
  input  in_13,
  input  in_14,
  input  in_15,
  input  in_16,
  input  in_17,
  output out_18,
  output out_19,
  output [2:0] out_20,
  output out_21,
  output [2:0] out_22,
  output [1:0] out_23
);

  wire not_1_out, or_5_out, or_6_out, or_7_out, or_8_out;
  wire [1:0] or_1_out;
  wire [2:0] or_2_out;

  not not_1 (not_1_out, in_14);
  or or_1 (or_1_out[0], in_15, in_14);
  or or_2 (or_2_out[0], in_4, in_3, in_7, in_11, in_9, in_13);
  or or_3 (or_2_out[1], in_13, in_7, in_5, in_8, in_9, in_12);
  or or_4 (or_2_out[2], in_6, in_8, in_4, in_9);
  or or_5 (or_5_out, in_10, in_11, in_12, in_13);
  and and_1 (out_21, or_5_out, in_1);
  and and_2 (or_1_out[1], in_15, not_1_out);
  assign out_23 = {1'b0, in_16} & {2{in_1}};  // AND_Gate and_3, 2 bits wide
  or or_6 (or_6_out, or_2_out[0], or_2_out[1], or_2_out[2]);
  or or_7 (or_7_out, in_2, or_6_out);
  assign out_20 = or_2_out & {3{in_1}};  // AND_Gate and_4, 3 bits wide
  assign out_22 = {in_14, or_1_out} & {3{in_1}};  // AND_Gate and_5, 3 bits wide
  or or_8 (or_8_out, or_7_out, in_14, in_15);
  and and_6 (out_19, or_8_out, ~in_11, ~in_12, ~in_13, in_1);  // AND_Gate

  assign out_18 = in_1;

  // Other names for the same wires on the sheet: jr = in_16; mfhi = in_14; EN = in_1; PC = in_1; add = in_2;
  //   and = in_4; div = in_12; divu = in_13; LH = out_21; mflo = in_15; mul = in_10; mulu = in_11; nop = in_17;
  //   nor = in_7; or = in_5; Rf_Rw = out_19; S_ALU[2:0] = out_20; S_BC[1:0] = out_23; S_Di[2:0] = out_22; slt = in_8;
  //   sltu = in_9; sub = in_3; xor = in_6
endmodule

module Type_Inm_Decoder (
  input  in_1,
  input  in_2,
  input  in_3,
  input  in_4,
  input  in_5,
  input  in_6,
  input  in_7,
  output [2:0] out_8,
  output [1:0] out_9,
  output out_10,
  output out_11,
  output out_12
);

  wire or_1_out;
  wire [1:0] or_3_out;
  wire [2:0] or_4_out;

  or or_1 (or_1_out, in_2, in_3, in_4, in_5, in_6, in_7);
  or or_2 (or_3_out[1], in_3, in_4, in_5);
  or or_3 (or_3_out[0], in_6, in_7, in_2);
  and and_1 (out_10, or_1_out, in_1);
  assign out_9 = or_3_out & {2{in_1}};  // AND_Gate and_2, 2 bits wide
  or or_4 (or_4_out[0], in_3, in_7);
  or or_5 (or_4_out[1], in_4, in_7, in_6);
  or or_6 (or_4_out[2], in_3, in_6, in_7, in_5);
  assign out_8 = or_4_out & {3{in_1}};  // AND_Gate and_3, 3 bits wide

  assign out_11 = in_1;
  assign out_12 = in_1;

  // Other names for the same wires on the sheet: En = in_1; PC = in_1; RW_RF = in_1; addi = in_2; andi = in_3;
  //   ori = in_4; S_ALU[2:0] = out_8; S_B[1:0] = out_9; S_DA = out_10; slti = in_6; sltiu = in_7; xori = in_5
endmodule

module Type_Stack (
  input  in_1,
  input  in_2,
  input  in_3,
  input  in_4,
  input  Rst,
  input  in_6,
  output out_7,
  output out_8,
  output out_9,
  output [1:0] out_10,
  output out_11,
  output out_12,
  output out_13,
  output out_14,
  output [1:0] out_15,
  output [2:0] out_16,
  output [2:0] out_17,
  output out_18
);

  wire d_ff_1_q, d_ff_3_q, demultiplexer_1_out0, demultiplexer_2_out0, EndPop, EndPush, PCpush, S_Adr1pop,
       startRampop, startRampush;

  or or_1 (out_12, out_7, out_17[0]);
  or or_2 (out_15[1], out_7, out_17[0]);
  and and_1 (startRampop, in_3, in_1);
  D_Flip_Flop d_ff_1 (.clk(in_6), .D(demultiplexer_1_out0), .Q(d_ff_1_q), .reset(Rst));  // open: Qn, preset, en
  and and_2 (out_17[0], in_3, in_2);
  or or_3 (S_Adr1pop, startRampop, d_ff_1_q);
  or or_4 (out_10[1], S_Adr1pop, out_8);
  or or_5 (out_18, out_7, out_17[0]);
  Demultiplexer #(.enable("false")) demultiplexer_1 (
    .out0(demultiplexer_1_out0), .out1(out_7), .in(S_Adr1pop), .sel(in_4));
  D_Flip_Flop d_ff_2 (.clk(in_6), .D(out_17[0]), .Q(startRampush), .reset(Rst));  // open: Qn, preset, en
  D_Flip_Flop d_ff_3 (.clk(in_6), .D(demultiplexer_2_out0), .Q(d_ff_3_q), .reset(Rst));  // open: Qn, preset, en
  or or_6 (out_13, out_7, PCpush);
  or or_7 (out_8, startRampush, d_ff_3_q);
  or or_8 (out_11, startRampop, startRampush);
  D_Flip_Flop d_ff_4 (.clk(in_6), .D(out_7), .Q(EndPop), .reset(Rst));  // open: Qn, preset, en
  Demultiplexer #(.enable("false")) demultiplexer_2 (
    .out0(demultiplexer_2_out0), .out1(PCpush), .in(out_8), .sel(in_4));
  or or_9 (out_14, EndPop, EndPush);
  D_Flip_Flop d_ff_5 (.clk(in_6), .D(PCpush), .Q(EndPush), .reset(Rst));  // open: Qn, preset, en

  assign out_9 = out_8;
  assign out_10[0] = 1'b0;
  assign out_15[0] = out_15[1];
  assign out_16 = {2'b00, out_7};
  assign out_17[2:1] = 2'b00;

  // Other names for the same wires on the sheet: Clk = in_6; En = in_3; ENDStack = out_14; PC = out_13; pop = in_1;
  //   push = in_2; RamReady = in_4; S_A = out_12; S_Adr[1] = out_10[1]; S_ALU[0] = out_17[0]; S_ALU0 = out_17[0];
  //   S_Apush = out_17[0]; S_Bpush = out_17[0]; SP_RWpush = out_17[0]; S_B[1:0] = {2{out_15[1]}}; PCpop = out_7;
  //   Rf_Rw = out_7; S_Apop = out_7; S_Bpop = out_7; S_Di[0] = out_7; S_Di0 = out_7; SP_RWpop = out_7; RamW = out_8;
  //   S_Adr1push = out_8; S_Do = out_8; SP_RW = out_18; startRam = out_11

  // Notes on the sheet:
  //   POP
  //   PUSH
endmodule

module Type_Branch (
  input  in_1,
  input  in_2,
  input  in_3,
  input  in_4,
  input  in_5,
  input  in_6,
  input  in_7,
  output out_8,
  output [2:0] out_9,
  output [1:0] out_10,
  output [2:0] out_11
);

  wire [0:0] or_3_out;
  wire [1:0] or_2_out;
  wire [1:1] or_4_out;

  or or_1 (or_2_out[1], in_5, in_4);
  or or_2 (or_2_out[0], in_5, in_3);
  or or_3 (or_3_out[0], in_2, in_3, in_4, in_5, in_6);
  or or_4 (or_4_out[1], or_3_out[0], in_7);
  assign out_10 = {or_4_out[1], or_3_out[0]} & {2{in_1}};  // AND_Gate and_1, 2 bits wide
  assign out_11 = {in_6, or_2_out} & {3{in_1}};  // AND_Gate and_2, 3 bits wide
  assign out_9 = {2'b00, or_3_out[0]} & {3{in_1}};  // AND_Gate and_3, 3 bits wide

  assign out_8 = in_1;

  // Other names for the same wires on the sheet: bltz = in_6; EN = in_1; PC = in_1; beq = in_2; bgtz = in_5;
  //   blez = in_4; bne = in_3; jmp = in_7; S_ALU[2:0] = out_9; S_BC[1:0] = out_10; S_flags[2:0] = out_11
endmodule

module Type_Word (
  input  in_1,
  input  in_2,
  input  in_3,
  input  Rst,
  input  in_5,
  input  in_6,
  output out_7,
  output out_8,
  output out_9,
  output out_10,
  output [1:0] out_11,
  output out_12,
  output [1:0] out_13,
  output [2:0] out_14,
  output out_15
);

  wire d_ff_1_q, d_ff_2_q, demultiplexer_1_out0, demultiplexer_2_out0, EndLW, EndSW, PCs, S_Adr0l, startRaml,
       startRams;

  and and_1 (startRaml, in_1, in_3);
  D_Flip_Flop d_ff_1 (.clk(in_2), .D(demultiplexer_1_out0), .Q(d_ff_1_q), .reset(Rst));  // open: Qn, preset, en
  and and_2 (startRams, in_1, in_6);
  D_Flip_Flop d_ff_2 (.clk(in_2), .D(demultiplexer_2_out0), .Q(d_ff_2_q));  // open: Qn, preset, en, reset
  or or_1 (S_Adr0l, startRaml, d_ff_1_q);
  or or_2 (out_12, startRams, d_ff_2_q);
  Demultiplexer #(.enable("false")) demultiplexer_1 (
    .out0(demultiplexer_1_out0), .out1(out_7), .in(S_Adr0l), .sel(in_5));
  Demultiplexer #(.enable("false")) demultiplexer_2 (.out0(demultiplexer_2_out0), .out1(PCs), .in(out_12), .sel(in_5));
  D_Flip_Flop d_ff_3 (.clk(in_2), .D(PCs), .Q(EndSW), .reset(Rst));  // open: Qn, preset, en
  D_Flip_Flop d_ff_4 (.clk(in_2), .D(out_7), .Q(EndLW), .reset(Rst));  // open: Qn, preset, en
  or or_3 (out_9, EndLW, EndSW);
  or or_4 (out_10, startRaml, startRams);
  or or_5 (out_11[0], out_12, S_Adr0l);
  or or_6 (out_13[0], S_Adr0l, out_12);
  or or_7 (out_15, out_7, PCs);

  assign out_8 = out_7;
  assign out_11[1] = 1'b0;
  assign out_13[1] = 1'b0;
  assign out_14 = {2'b00, out_7};

  // Other names for the same wires on the sheet: Clk = in_2; EN = in_1; ENDw = out_9; LoadWord = in_3; PC = out_15;
  //   RamReady = in_5; S_Adr[0] = out_13[0]; S_B[0] = out_11[0]; S_B0l = S_Adr0l; RamW = out_12; S_Adr0s = out_12;
  //   S_B0s = out_12; PCl = out_7; Rf_Rw = out_7; S_DA = out_7; S_Di[0] = out_7; S_Di0 = out_7; startRam = out_10;
  //   StoreWord = in_6

  // Notes on the sheet:
  //   LOAD
  //   STORE
endmodule

module Type_Special (
  input  in_1,
  input  in_2,
  input  in_3,
  input  in_4,
  output out_5,
  output [2:0] out_6,
  output out_7,
  output out_8,
  output out_9
);

  wire [2:2] or_1_out;

  or or_1 (or_1_out[2], in_2, in_3);
  and and_1 (out_5, or_1_out[2], in_1);
  and and_2 (out_7, in_4, in_1);
  assign out_6 = {{2{or_1_out[2]}}, in_2} & {3{in_1}};  // AND_Gate and_3, 3 bits wide
  and and_4 (out_9, in_2, in_1);

  assign out_8 = in_1;

  // Other names for the same wires on the sheet: kbd = in_2; En = in_1; PC = in_1; kbdEn = out_9; Rf = out_5;
  //   rnd = in_3; S_Di[2:0] = out_6; tty = in_4; tty_Enable = out_7
endmodule
